# Fritzing sketch robotHouse (saved by Fritzing 0.9.4)
breadboards: 1

parts:
  元件1 = Arduino Uno (Rev3)
  S1 = Momentary Switch [package=tactile-pth]
  S2 = Momentary Switch [package=tactile-pth]
  S3 = Momentary Switch [package=tactile-pth]
  S4 = Momentary Switch [package=tactile-pth]
  S5 = Momentary Switch [package=tactile-pth]
  S6 = Momentary Switch [package=tactile-pth]
  LED1 = RGB LED - (4 legs) [package="5 mm [THT]"]
  R1 = Resistor [tolerance=±5% resistance=220 package="0805 [SMD]"]
  R2 = Resistor [tolerance=±5% resistance=220 package="0805 [SMD]"]
  R3 = Resistor [tolerance=±5% resistance=220 package="0805 [SMD]"]
  J1 = Basic Servo
  R4 = Resistor [tolerance=±5% resistance=10k package="0402 [SMD]"]
  LED2 = LEDs [package=led10mm]
  LED3 = LEDs [package=led10mm]
  LED4 = LEDs [package=led10mm]
  LED5 = LEDs [package=led10mm]
  LED6 = LEDs [package=led10mm]
  LED7 = LEDs [package=led10mm]
  LED8 = LEDs [package=led10mm]
  J2 = Piezo Speaker
  R5 = Resistor [tolerance=±5% resistance=100 package="1206 [SMD]"]

nets:
  N1: 元件1.D9_PWM, R1.Pin_1
  N2: 元件1.D10_PWM/SS, R5.Pin_0
  GND: 元件1.GND, S1.2, S5.2, S6.2, LED1.common_anode, J1.gnd, R4.Pin_1, LED2.C, LED3.C, LED4.C, LED8.C
  N3: 元件1.D2, S1.3, S2.3, S3.3, S4.3, S5.3, S6.3
  N4: 元件1.D5_PWM, R2.Pin_1
  N5: 元件1.D6_PWM, R3.Pin_1
  5V: 元件1.5V, S1.1, S2.1, S3.1, S4.1, S5.1, S6.1, J1.vcc, LED2.A, LED3.A, LED4.A, J2.pin1
  N6: S2.2, S3.2, S4.2, R4.Pin_0
  N7: LED1.red_cathode, R1.Pin_0
  N8: LED1.green_cathode, R3.Pin_0
  N9: LED1.blue_cathode, R2.Pin_0
  N10: LED5.C, LED6.C, LED7.C
  N11: LED5.A, LED6.A, LED7.A, LED8.A
  N12: J2.pin2, R5.Pin_1
